# Fritzing sketch racing_car_hat (saved by Fritzing 0.9.4)
perfboards: 1

parts:
  J5 = Raspberry Pi Header 40pin [form="♂ (male)" package=THT]
  JP3 = Header 6 [package=1x06_smd_straight_alt]
  R12 = Resistor [tolerance=±5% resistance=2k package=THT]
  R13 = Resistor [tolerance=±5% resistance=2k package=THT]
  R14 = Resistor [tolerance=±5% resistance=220 package=THT]
  U3 = 74HC595 [package="DIP16 [THT]"]
  R15 = Resistor [tolerance=±5% resistance=220 package=THT]
  R16 = Resistor [tolerance=±5% resistance=220 package=THT]
  R17 = Resistor [tolerance=±5% resistance=220 package=THT]
  LED6 = LED - 5mm [color="Green (555nm)" package="5 mm [THT]"]
  R18 = Resistor [tolerance=±5% resistance=220 package=THT]
  LED7 = LED - 5mm [color="Red (633nm)" package="5 mm [THT]"]
  LED8 = LED - 5mm [color="Red (633nm)" package="5 mm [THT]"]
  LED9 = LED - 5mm [color="Red (633nm)" package="5 mm [THT]"]
  Q1 = NPN-Transistor [package="TO92 [THT]"]
  R19 = Trimmer Potentiometer [maximum_resistance=10kΩ package=THT]
  J6 = female pin header, 2 pins [form="♀ (female)"]
  J3 = Piezo Speaker

nets:
  3V3: J5.3v3, J5.3V3, JP3.1, R14.Pin_1
  N1: J5.GIPO4, U3.DS
  N2: J5.GND, R12.Pin_1, R13.Pin_1, U3.OE
  N3: J5.GIPO17, U3.ST_CP
  N4: J5.GIPO27, U3.SH_CP
  N5: J5.GIPO5, JP3.2
  N6: J5.GIPO6, JP3.3
  N7: J5.GIPO13, JP3.5
  N8: J5.GIPO19, JP3.6
  5V: J5.5V, U3.VCC, R19.leg2
  N9: U3.Q1, R17.Pin_1
  N10: U3.Q2, R16.Pin_1
  N11: U3.Q3, R15.Pin_1
  N12: R15.Pin_0, LED6.anode
  N13: R16.Pin_0, LED9.anode
  N14: R17.Pin_0, LED8.anode
  N15: LED6.cathode, R19.leg1
  N16: R18.Pin_0, LED7.anode
  N17: Q1.C, R19.wiper
  N18: J6.pin1, J3.pin1
  N19: J6.pin2, J3.pin2

custom parts:
  Raspberry Pi Header 40pin: Raspberry Pi 40 pin header - for creating your own shields.
